// Logisim project Gated D latch.circ as structural Verilog: 1 circuit, main circuit main
module main (
  input  D,
  input  Clock,
  output Qa,
  output Qb
);

  wire nand_1_out, nand_2_out, not_1_out;

  not not_1 (not_1_out, D);
  nand nand_1 (nand_1_out, D, Clock);
  nand nand_2 (nand_2_out, Clock, not_1_out);
  nand nand_3 (Qa, nand_1_out, Qb);
  nand nand_4 (Qb, Qa, nand_2_out);
endmodule
